# Fritzing sketch BitBanger-LCD1 (saved by Fritzing 0.9.10b)
breadboards: 2

parts:
  LCD1 = LCD screen
  Part1 = Arduino Micro (Rev3)
  SW1 = DIP Switch 8 Position [package=dipswitch-08]
  R1 = TRIMPOT [maximum_resistance=10kΩ knob_status=50% power=0.5W package=trim_pot_pth]
  R2 = Resistor [tolerance=±5% power=0.25 resistance=220 package=THT]
  R3 = Resistor [tolerance=±5% power=0.25 resistance=220 package=THT]
  R4 = Resistor [tolerance=±5% power=0.25 resistance=220 package=THT]
  R5 = Resistor [tolerance=±5% power=0.25 resistance=220 package=THT]
  R6 = Resistor [tolerance=±5% power=0.25 resistance=220 package=THT]
  R7 = Resistor [tolerance=±5% power=0.25 resistance=10k package=THT]
  S1 = Pushbutton [package="[THT]"]
  S2 = Pushbutton [package="[THT]"]
  S3 = Pushbutton [package="[THT]"]
  S4 = Pushbutton [package="[THT]"]
  R8 = Resistor [tolerance=±5% power=0.25 resistance=10k package=THT]
  R9 = Resistor [tolerance=±5% power=0.25 resistance=10k package=THT]
  R11 = Resistor [tolerance=±5% power=0.25 resistance=220 package=THT]
  R12 = Resistor [tolerance=±5% power=0.25 resistance=220 package=THT]
  R13 = Resistor [tolerance=±5% power=0.25 resistance=220 package=THT]
  R14 = Resistor [tolerance=±5% power=0.25 resistance=220 package=THT]

nets:
  N1: LCD1.VSS, LCD1.R/W, LCD1.LED-, R2.Pin_0, R3.Pin_0, R4.Pin_0, R5.Pin_0, R6.Pin_0, R7.Pin_0, R8.Pin_0, R9.Pin_0, R11.Pin_0, R12.Pin_0, R13.Pin_0, R14.Pin_0
  VDD: LCD1.VDD, LCD1.LED+, Part1.5V, SW1.1, SW1.2, SW1.3, R1.CCW, R1.CW, S3.Pin_1, S3.Pin_2, S4.Pin_1, S4.Pin_2
  N2: LCD1.V0, R1.WIPER
  N3: LCD1.E, Part1.D13_PWM
  N4: Part1.MOSI, S1.Pin_1, S1.Pin_2, R11.Pin_1
  N5: Part1.RXLED/SS, S2.Pin_1, S2.Pin_2, R12.Pin_1
  N6: Part1.D2/SDA, SW1.10, R8.Pin_1
  N7: Part1.D3/SCL, SW1.9, R9.Pin_1
  N8: Part1.SCK, S4.Pin_3, S4.Pin_4, R13.Pin_1
  N9: Part1.MISO, S3.Pin_3, S3.Pin_4, R14.Pin_1
  N10: Part1.A5, SW1.16, R2.Pin_1
  N11: Part1.A4, SW1.15, R3.Pin_1
  N12: Part1.A3, SW1.14, R4.Pin_1
  N13: Part1.A2, SW1.13, R5.Pin_1
  N14: Part1.A1, SW1.12, R6.Pin_1
  N15: Part1.A0, SW1.11, R7.Pin_1
  N16: SW1.4, SW1.5
  N17: SW1.6, SW1.7, SW1.8
  N18: S1.Pin_3, S1.Pin_4
  N19: S2.Pin_3, S2.Pin_4
